# Fritzing sketch cathode (saved by Fritzing 0.7.10b)
breadboards: 1

parts:
  Arduino1 = Arduino
  R1 = Resistor [tolerance=±5% resistance=220 package=THT]
  R2 = Resistor [tolerance=±5% resistance=220 package=THT]
  R3 = Resistor [tolerance=±5% resistance=220 package=THT]
  LED1 = RGB LED (com. cathode, rbg) [package="5 mm [THT]"]

nets:
  N1: Arduino1.GND, LED1.common_cathode
  N2: Arduino1.D11, R1.Pin_0
  N3: Arduino1.D10, R2.Pin_0
  N4: Arduino1.D9, R3.Pin_0
  N5: R1.Pin_1, LED1.red_anode
  N6: R2.Pin_1, LED1.blue_anode
  N7: R3.Pin_1, LED1.green_anode
