# Fritzing sketch dht22 (saved by Fritzing 0.7.11b)
breadboards: 1

parts:
  RHT1 = Humidity and Temperature Sensor RHT03
  Arduino1 = Arduino
  R1 = 4.7k Ω Resistor [package=THT]

nets:
  VCC: RHT1.Vcc, Arduino1.3V3, R1.Pin_0
  N1: RHT1.Data-signal, Arduino1.D13, R1.Pin_1
  N2: RHT1.GND_1, RHT1.GND_2, Arduino1.GND
