# Fritzing sketch keypad (saved by Fritzing 0.7.10b)
breadboards: 1

parts:
  Arduino1 = Arduino
  R1 = 1k Ω Resistor [package=THT]
  R2 = 1k Ω Resistor [package=THT]
  R3 = 1k Ω Resistor [package=THT]
  R4 = 1k Ω Resistor [package=THT]
  kEYPAD_MATRICIAL_1 = KEYPAD 4x3

nets:
  N1: Arduino1.D12, kEYPAD_MATRICIAL_1.col1
  N2: Arduino1.D7, kEYPAD_MATRICIAL_1.arrow1
  N3: Arduino1.D6, R4.Pin_0, kEYPAD_MATRICIAL_1.col2
  N4: Arduino1.D5, kEYPAD_MATRICIAL_1.arrow2
  N5: Arduino1.D4, R3.Pin_0, kEYPAD_MATRICIAL_1.col3
  N6: Arduino1.D3, R2.Pin_0, kEYPAD_MATRICIAL_1.arrow3
  N7: Arduino1.D2, R1.Pin_0, kEYPAD_MATRICIAL_1.arrow4
  N8: Arduino1.+5V, R1.Pin_1, R2.Pin_1, R3.Pin_1, R4.Pin_1

custom parts:
  KEYPAD 4x3: KEYPAD matricial de 12 botones, 4 filas x 3 columnas
