# Fritzing sketch led (saved by Fritzing 0.7.10b)
breadboards: 1

parts:
  Arduino1 = Arduino
  R1 = Resistor [tolerance=±5% resistance=220 package=THT]
  LED1 = red smd LED [package="1206 [SMD]"]

nets:
  N1: Arduino1.GND, LED1.cathode
  N2: Arduino1.D13, R1.Pin_1
  N3: R1.Pin_0, LED1.anode
