# Fritzing sketch sht1x (saved by Fritzing 0.7.10b)
breadboards: 1

parts:
  Arduino1 = Arduino
  Part1 = Humidity Temperature Sensor SHT15

nets:
  GND: Arduino1.GND, Part1.GND
  N1: Arduino1.D11, Part1.SCL
  N2: Arduino1.D10, Part1.SDA
  +5V: Arduino1.+5V, Part1.VCC
